# Fritzing sketch akbil (saved by Fritzing 0.9.2b)
breadboards: 2

parts:
  LCD1 = LCD screen
  Eleman1 = RFID-RC522-v2
  Raspberry_Pi1 = Raspberry Pi 2
  LED1 = smd LED [color="Red (633nm)" package="1206 [SMD]"]
  LED2 = smd LED [color="Red (633nm)" package="1206 [SMD]"]
  R1 = Resistor [tolerance=±5% resistance=220 package="0603 [SMD]"]
  R2 = Resistor [tolerance=±5% resistance=220 package="0603 [SMD]"]
  J1 = Piezo Speaker

nets:
  GND: LCD1.VSS, LCD1.LED-, Eleman1.IRQ, Eleman1.GND, Raspberry_Pi1.GND, LED1.cathode, LED2.cathode, J1.pin1
  VDD: LCD1.VDD, Raspberry_Pi1.5V
  N1: LCD1.RS, Raspberry_Pi1.GPIO7
  N2: LCD1.R/W, LCD1.LED+, R1.Pin_1, R2.Pin_1
  N3: LCD1.E, Raspberry_Pi1.GPIO20
  N4: LCD1.DB4, Raspberry_Pi1.GPIO13
  N5: LCD1.DB5, Raspberry_Pi1.GPIO24
  N6: LCD1.DB6, Raspberry_Pi1.GPIO23
  N7: LCD1.DB7, Raspberry_Pi1.GPIO18
  N8: Eleman1.SDA, Raspberry_Pi1.GPIO8
  N9: Eleman1.SCK, Raspberry_Pi1.GPIO11
  N10: Eleman1.MOSI, Raspberry_Pi1.GPIO10
  N11: Eleman1.MISO, Raspberry_Pi1.GPIO9
  N12: Eleman1.RST, Raspberry_Pi1.GPIO25
  3.3V: Eleman1.3.3V, Raspberry_Pi1.3v3
  N13: Raspberry_Pi1.GPIO21, J1.pin2
  N14: LED1.anode, R1.Pin_0
  N15: LED2.anode, R2.Pin_0

custom parts:
  RFID-RC522-v2: A simple China made RFID-RC522 Reader; do check the pin labels, as this is a MFRC522 based clone.
